# Fritzing sketch OpenDoor (saved by Fritzing 0.8.7b)
circuit board: 8.46667cm x 5.64444cm
breadboards: 1

parts:
  kEYPAD_MATRICIAL_1 = KEYPAD 4x3
  R3 = Resistor [tolerance=±5% resistance=1k package=THT]
  R4 = Resistor [tolerance=±5% resistance=1k package=THT]
  R6 = Resistor [tolerance=±5% resistance=1k package=THT]
  S1 = Reed switch [package=THT]
  R8 = Resistor [tolerance=±5% resistance=1k package=THT]
  R7 = Resistor [tolerance=±5% resistance=1k package=THT]
  LED1 = LED - 5mm [color="White (8000K)" package="5 mm [THT]"]
  R9 = Resistor [tolerance=±5% resistance=1k package=THT]

nets:
  N1: kEYPAD_MATRICIAL_1.arrow1, R3.Pin_0
  N2: kEYPAD_MATRICIAL_1.arrow2, R4.Pin_0
  N3: kEYPAD_MATRICIAL_1.arrow3, R6.Pin_0
  N4: kEYPAD_MATRICIAL_1.arrow4, R7.Pin_0
  GND: R3.Pin_1, R4.Pin_1, R6.Pin_1, R8.Pin_1, R7.Pin_1, R9.Pin_1
  N5: S1.pin_2, R8.Pin_0
  N6: LED1.cathode, R9.Pin_0

custom parts:
  KEYPAD 4x3: KEYPAD matricial de 12 botones, 4 filas x 3 columnas
